// Digital circuit 4bit_Processor.dlogic.dig as structural Verilog
module _4bit_Processor_dlogic (
  input  [3:0] in_4,
  input  [3:0] in_5,
  input  in_6,
  input  [1:0] in_7,
  input  [1:0] in_8,
  input  clk,
  input  in_16,
  output out_1,
  output out_2,
  output out_3,
  output [3:0] out_10,
  output [3:0] out_11,
  output [3:0] out_12,
  output out_13,
  output out_14,
  output out_15
);

  wire cu_1_p5, cu_1_p7, cu_1_p8, cu_1_p9, cu_1_p10, cu_1_p12, cu_1_p13, cu_1_p14, cu_1_p15, cu_1_p16,
       instructionregister_1_p4, instructionregister_1_p5, instructionregister_1_p6,
       instructionregister_1_p7, programcounter_1_p5;
  wire [0:0] fetchdecodeexecute_1_p3;
  wire [2:0] or_2_out;
  wire [3:0] multiplexer_1_out, ram_1_p5;

  // ProgramCounter programcounter_1: pin names not known; wires that end beside it: clk, in_7, in_5, in_6, programcounter_1_p5
  // FetchDecodeExecute fetchdecodeexecute_1: pin names not known; wires that end beside it: clk, in_16, fetchdecodeexecute_1_p3[0], out_14, out_15
  // RAM ram_1: pin names not known; wires that end beside it: in_8, clk, programcounter_1_p5, in_4, ram_1_p5
  // InstructionRegister instructionregister_1: pin names not known; wires that end beside it: clk, {1'b0, fetchdecodeexecute_1_p3[0]}, ram_1_p5, instructionregister_1_p4, instructionregister_1_p5, instructionregister_1_p6, instructionregister_1_p7
  // CU cu_1: pin names not known; wires that end beside it: instructionregister_1_p5, instructionregister_1_p4, instructionregister_1_p6, instructionregister_1_p7, cu_1_p5, 1'b0, cu_1_p7, cu_1_p8, cu_1_p9, cu_1_p10, out_13, cu_1_p12, cu_1_p13, cu_1_p14, cu_1_p15, cu_1_p16
  or or_1 (or_2_out[0], cu_1_p12, cu_1_p16, cu_1_p7);
  or or_2 (or_2_out[1], cu_1_p8, cu_1_p16);
  or or_3 (or_2_out[2], cu_1_p10, cu_1_p7);
  Multiplexer #(.Bits(4)) multiplexer_1 (.sel(cu_1_p15), .in_0(out_10), .in_1(ram_1_p5), .out(multiplexer_1_out));
  // RegisterFile registerfile_1: pin names not known; wires that end beside it: cu_1_p9, cu_1_p5, clk, multiplexer_1_out, cu_1_p13, cu_1_p14, out_12, out_11
  // _4bit_ALU_dlogic _4bit_alu_dlogic_1: pin names not known; wires that end beside it: out_12, out_11, or_2_out, out_10, out_1, out_2, out_3
endmodule
